# Fritzing sketch AdMechBoard (saved by Fritzing 0.9.3b)
circuit board: 8.46667cm x 5.64444cm
breadboards: 1

parts:
  R4 = Resistor [tolerance=±5% resistance=10k package=THT]
  R5 = Resistor [tolerance=±5% resistance=10k package=THT]
  R6 = Resistor [tolerance=±5% resistance=10k package=THT]
  R7 = Resistor [tolerance=±5% resistance=10k package=THT]
  R8 = Resistor [tolerance=±5% resistance=10k package=THT]
  R9 = Resistor [tolerance=±5% resistance=10k package=THT]
  R10 = Resistor [tolerance=±5% resistance=10k package=THT]
  R11 = Resistor [tolerance=±5% resistance=10k package=THT]
  R12 = Resistor [tolerance=±5% resistance=10k package=THT]
  Raspberry_Pi_1 = Raspberry Pi 3 [part_number=RPI-3-V1.2]
  plusButton = Pushbutton [package="[THT]"]
  minusButton = Pushbutton [package="[THT]"]
  okButton = Pushbutton [package="[THT]"]
  LED1 = LED - 5mm [color="Red (633nm)" package="5 mm [THT]"]
  LED2 = LED - 5mm [color="Red (633nm)" package="5 mm [THT]"]
  LED3 = LED - 5mm [color="Red (633nm)" package="5 mm [THT]"]
  LED4 = LED - 5mm [color="Red (633nm)" package="5 mm [THT]"]
  LED5 = LED - 5mm [color="Red (633nm)" package="5 mm [THT]"]
  LED6 = LED - 5mm [color="Red (633nm)" package="5 mm [THT]"]
  LED7 = LED - 5mm [color="Red (633nm)" package="5 mm [THT]"]
  LED8 = LED - 5mm [color="Red (633nm)" package="5 mm [THT]"]
  LED9 = LED - 5mm [color="Red (633nm)" package="5 mm [THT]"]
  LED10 = LED - 5mm [color="Red (633nm)" package="5 mm [THT]"]
  LED11 = LED - 5mm [color="Red (633nm)" package="5 mm [THT]"]
  LED12 = LED - 5mm [color="Red (633nm)" package="5 mm [THT]"]
  R1 = Resistor [tolerance=±20% resistance=10k package=THT]
  R2 = Resistor [tolerance=±5% resistance=10k package=THT]
  R3 = Resistor [tolerance=±5% resistance=10k package=THT]

nets:
  N1: R4.Pin_0, LED4.anode
  N2: R4.Pin_1, Raspberry_Pi_1.GPIO19
  N3: R5.Pin_0, LED5.anode
  N4: R5.Pin_1, Raspberry_Pi_1.GPIO26
  N5: R6.Pin_0, LED6.anode
  N6: R6.Pin_1, Raspberry_Pi_1.GPIO21
  N7: R7.Pin_0, LED7.anode
  N8: R7.Pin_1, Raspberry_Pi_1.GPIO23
  N9: R8.Pin_0, LED8.anode
  N10: R8.Pin_1, Raspberry_Pi_1.GPIO24
  N11: R9.Pin_0, LED9.anode
  N12: R9.Pin_1, Raspberry_Pi_1.GPIO25
  N13: R10.Pin_0, LED10.anode
  N14: R10.Pin_1, Raspberry_Pi_1.GPIO12
  N15: R11.Pin_0, LED11.anode
  N16: R11.Pin_1, Raspberry_Pi_1.GPIO16
  N17: R12.Pin_0, LED12.anode
  N18: R12.Pin_1, Raspberry_Pi_1.GPIO20
  N19: Raspberry_Pi_1.GPIO17, plusButton.Pin_4
  N20: Raspberry_Pi_1.GPIO27, minusButton.Pin_4
  N21: Raspberry_Pi_1.GPIO22, okButton.Pin_4
  N22: Raspberry_Pi_1.GPIO5, R1.Pin_1
  N23: Raspberry_Pi_1.GPIO6, R2.Pin_1
  N24: Raspberry_Pi_1.GPIO13, R3.Pin_1
  N25: Raspberry_Pi_1.GND, plusButton.Pin_1, plusButton.Pin_2, minusButton.Pin_1, minusButton.Pin_2, okButton.Pin_1, okButton.Pin_2, LED1.cathode, LED2.cathode, LED3.cathode, LED4.cathode, LED5.cathode, LED6.cathode, LED7.cathode, LED8.cathode, LED9.cathode, LED10.cathode, LED11.cathode, LED12.cathode
  N26: LED1.anode, R1.Pin_0
  N27: LED2.anode, R2.Pin_0
  N28: LED3.anode, R3.Pin_0

notes:
  gpio17
  gpio27
  gpio22
  gpio6
  gpio13
  gpio5
  gpio21
  gpio19
  gpio26
  gpio20
  gpio16
  gpio23
  gpio12
  gpio24
  gpio25
  GND
